# Fritzing sketch hookup_diagram_step_1 (saved by Fritzing 0.8.7b)
breadboards: 1

parts:
  BeagleBone1 = BeagleBone Black
  J1 = Piezo Speaker

nets:
  N1: BeagleBone1.no_name_yet#1, J1.pin2
  N2: BeagleBone1.no_name_yet#14, J1.pin1

custom parts:
  BeagleBone Black: BeagleBone Black rev. A5B
